# Fritzing sketch led_wifi_module (saved by Fritzing 0.9.3b)
breadboards: 1

parts:
  U2 = NodeMCU V1.0
  LED1 = smd LED [color="Red (633nm)" package="0805 [SMD]"]
  LED2 = smd LED [color="Red (633nm)" package="0805 [SMD]"]
  VCC1 = Battery block 9V
  R1 = Resistor [tolerance=±5% resistance=220 package="2010 [SMD]"]
  R2 = Resistor [tolerance=±5% resistance=220 package=THT]

nets:
  N1: U2.D5, LED1.cathode
  N2: U2.D6, LED2.cathode
  N3: U2.Vin, VCC1.+
  N4: U2.GND, VCC1.-, R1.Pin_1, R2.Pin_1

custom parts:
  NodeMCU V1.0: ESP8266 based NodeMCU
